// Logisim project SLL8 - SRA1 se anulando e com indeterminação.circ as structural Verilog: 1 circuit, main circuit main
module main (
  input  SLL8,
  input  SRA1,
  output out_3,
  output out_4
);

  wire not_1_out, not_2_out;

  and and_1 (out_3, SLL8, not_1_out);
  not not_1 (not_1_out, SRA1);
  not not_2 (not_2_out, SLL8);
  and and_2 (out_4, not_2_out, SRA1);
endmodule
