// Logisim project parte1.circ as structural Verilog: 1 circuit, main circuit main
module main (
  input  in_1,
  input  in_2,
  input  in_3,
  input  in_4,
  input  in_5,
  input  in_6,
  input  in_7,
  input  in_8,
  input  C,
  input  Receptor_1,
  input  receptor_2,
  input  receptor_3,
  input  receptor_4,
  input  receptor_5,
  input  receptor_6,
  input  receptor_7,
  input  receptor_8,
  output C_2,
  output ENVIANDO,
  output out_20,
  output out_21,
  output out_22,
  output out_23,
  output out_24,
  output out_25,
  output out_26,
  output out_27
);

  wire and_1_out, and_2_out, and_3_out, and_4_out, and_5_out, and_6_out, and_7_out, and_8_out, and_9_out,
       and_10_out, and_11_out, and_12_out, and_13_out, and_14_out, not_1_out;

  not not_1 (not_1_out, C);
  and and_1 (and_1_out, in_1, C);
  and and_2 (and_2_out, not_1_out, in_2);
  and and_3 (and_3_out, in_2, C);
  or or_1 (out_21, and_1_out, receptor_2);
  and and_4 (and_4_out, not_1_out, in_3);
  or or_2 (out_22, and_3_out, receptor_3);
  and and_5 (and_5_out, not_1_out, in_4);
  and and_6 (and_6_out, in_3, C);
  and and_7 (and_7_out, in_4, C);
  or or_3 (out_23, and_6_out, receptor_4);
  and and_8 (and_8_out, not_1_out, in_5);
  or or_4 (out_24, and_7_out, receptor_5);
  and and_9 (and_9_out, in_5, C);
  and and_10 (and_10_out, not_1_out, in_6);
  and and_11 (and_11_out, in_6, C);
  or or_5 (out_25, and_9_out, receptor_6);
  and and_12 (and_12_out, not_1_out, in_7);
  or or_6 (out_26, and_11_out, receptor_7);
  and and_13 (and_13_out, not_1_out, in_8);
  and and_14 (and_14_out, in_7, C);
  and and_15 (ENVIANDO, in_8, C);
  or or_7 (out_27, and_14_out, receptor_8);

  assign C_2 = C;
  assign out_20 = Receptor_1;
endmodule
