// Logisim project parte4.circ as structural Verilog: 1 circuit, main circuit main
module main (
  input  in_1,
  input  in_2,
  input  in_3,
  input  in_4,
  input  in_5,
  input  in_6,
  input  in_7,
  input  in_8,
  input  C,
  input  RCEBENDO,
  output env_1,
  output env_2,
  output env_3,
  output out_14,
  output out_15,
  output out_16,
  output out_17,
  output out_18,
  output out_19,
  output out_20,
  output out_21,
  output env_4,
  output env_5,
  output env_6,
  output env_7,
  output env_8
);

  wire and_2_out, and_4_out, and_6_out, and_8_out, and_10_out, and_12_out, not_1_out;

  not not_1 (not_1_out, C);
  and and_1 (env_1, not_1_out, in_1);
  and and_2 (and_2_out, in_1, C);
  buf or_1 (out_14, RCEBENDO);  // OR_Gate
  and and_3 (env_2, not_1_out, in_2);
  and and_4 (and_4_out, in_2, C);
  buf or_2 (out_15, and_2_out);  // OR_Gate
  and and_5 (env_3, not_1_out, in_3);
  and and_6 (and_6_out, in_3, C);
  buf or_3 (out_16, and_4_out);  // OR_Gate
  and and_7 (env_4, not_1_out, in_4);
  and and_8 (and_8_out, in_4, C);
  buf or_4 (out_17, and_6_out);  // OR_Gate
  and and_9 (env_5, not_1_out, in_5);
  and and_10 (and_10_out, in_5, C);
  buf or_5 (out_18, and_8_out);  // OR_Gate
  and and_11 (env_6, not_1_out, in_6);
  and and_12 (and_12_out, in_6, C);
  buf or_6 (out_19, and_10_out);  // OR_Gate
  and and_13 (out_21, in_7, C);
  and and_14 (env_7, not_1_out, in_7);
  buf or_7 (out_20, and_12_out);  // OR_Gate
  and and_15 (env_8, not_1_out, in_8);
endmodule
