// Logisim project DESLOCADOR COM MUX COMPLETO DE 32 BITS.circ as structural Verilog: 1 circuit, main circuit main
module main (
  input  SRA1,
  input  SLL8,
  input  in_3,
  input  in_4,
  input  in_5,
  input  in_6,
  input  in_7,
  input  in_8,
  input  in_9,
  input  in_10,
  input  in_11,
  input  in_12,
  input  in_13,
  input  in_14,
  input  in_15,
  input  in_16,
  input  in_17,
  input  in_18,
  input  in_19,
  input  in_20,
  input  in_21,
  input  in_22,
  input  in_23,
  input  in_24,
  input  in_25,
  input  in_26,
  input  in_27,
  input  in_28,
  input  in_29,
  input  in_30,
  input  in_31,
  input  in_32,
  input  in_33,
  input  in_34,
  output out_35,
  output out_36,
  output out_37,
  output out_38,
  output out_39,
  output out_40,
  output out_41,
  output out_42,
  output out_43,
  output out_44,
  output out_45,
  output out_46,
  output out_47,
  output out_48,
  output out_49,
  output out_50,
  output out_51,
  output out_52,
  output out_53,
  output out_54,
  output out_55,
  output out_56,
  output out_57,
  output out_58,
  output out_59,
  output out_60,
  output out_61,
  output out_62,
  output out_63,
  output out_64,
  output out_65,
  output out_66
);

  wire main_1_c, parte_1_decodificador_1_p2, parte_1_decodificador_1_p4, parte_1_decodificador_1_p6,
       parte_1_decodificador_1_p8, parte_1_decodificador_1_p10, parte_1_decodificador_1_p12,
       parte_1_decodificador_1_p14, parte_1_decodificador_1_p16, undriven, undriven_2, undriven_3,
       undriven_4, undriven_5, undriven_6, undriven_7, undriven_8, undriven_9, undriven_10, undriven_11,
       undriven_12, undriven_13, undriven_14, undriven_15, undriven_16, undriven_17, undriven_18,
       undriven_19, undriven_20, undriven_21, undriven_22, undriven_23, undriven_24;

  filtro_das_chaves_seletoras_with_head_main main_1 (
    .IN(in_3), .IN_2(in_4), .IN_3(in_5), .IN_4(in_6), .OUT(undriven), .OUT_2(undriven_2), .OUT_3(undriven_3),
    .OUT_4(undriven_4), .IN_5(in_7), .IN_6(in_8), .IN_7(in_9), .IN_8(in_10), .OUT_5(undriven_5),
    .OUT_6(undriven_6), .OUT_7(undriven_7), .OUT_8(undriven_9), .IN_9(in_11), .IN_10(in_12), .IN_11(in_13),
    .IN_12(in_14), .OUT_9(undriven_10), .OUT_10(undriven_12), .OUT_11(undriven_13), .OUT_12(undriven_14),
    .IN_13(in_15), .IN_14(in_16), .IN_15(in_17), .IN_16(in_18), .OUT_13(undriven_15), .OUT_14(undriven_16),
    .OUT_15(undriven_17), .OUT_16(undriven_18), .OUTPUT(out_35), .OUTPUT_2(out_36), .OUTPUT_3(out_37),
    .OUTPUT_4(out_38), .OUTPUT_5(out_39), .OUTPUT_6(out_40), .OUTPUT_7(out_41), .OUTPUT_8(out_42),
    .OUTPUT_9(out_43), .OUTPUT_10(out_44), .OUTPUT_11(out_45), .OUTPUT_12(out_46), .OUTPUT_13(out_47),
    .OUTPUT_14(out_48), .OUTPUT_15(out_49), .OUTPUT_16(out_50), .C(main_1_c), .SRA1(SRA1), .SLL8(SLL8));
  filtro_das_chaves_seletoras_with_head_main main_2 (
    .IN(in_19), .IN_2(in_20), .IN_3(in_21), .IN_4(in_22), .OUT(undriven_19), .OUT_2(undriven_20),
    .OUT_3(undriven_21), .OUT_4(undriven_8), .IN_5(in_23), .IN_6(in_24), .IN_7(in_25), .IN_8(in_26),
    .OUT_5(undriven_11), .OUT_6(undriven_22), .OUT_7(undriven_23), .OUT_8(undriven_24), .IN_9(in_27),
    .IN_10(in_28), .IN_11(in_29), .IN_12(in_30), .OUT_9(parte_1_decodificador_1_p2),
    .OUT_10(parte_1_decodificador_1_p4), .OUT_11(parte_1_decodificador_1_p6),
    .OUT_12(parte_1_decodificador_1_p8), .IN_13(in_31), .IN_14(in_32), .IN_15(in_33), .IN_16(in_34),
    .OUT_13(parte_1_decodificador_1_p10), .OUT_14(parte_1_decodificador_1_p12),
    .OUT_15(parte_1_decodificador_1_p14), .OUT_16(parte_1_decodificador_1_p16), .OUTPUT(out_51),
    .OUTPUT_2(out_52), .OUTPUT_3(out_53), .OUTPUT_4(out_54), .OUTPUT_5(out_55), .OUTPUT_6(out_56),
    .OUTPUT_7(out_57), .OUTPUT_8(out_58), .OUTPUT_9(out_59), .OUTPUT_10(out_60), .OUTPUT_11(out_61),
    .OUTPUT_12(out_62), .OUTPUT_13(out_63), .OUTPUT_14(out_64), .OUTPUT_15(out_65), .OUTPUT_16(out_66),
    .C(main_1_c), .SRA1(SRA1), .SLL8(SLL8));
  // parte_1_Decodificador parte_1_decodificador_1: pin names not known; wires that end beside it: in_27, parte_1_decodificador_1_p2, in_28, parte_1_decodificador_1_p4, in_29, parte_1_decodificador_1_p6, in_30, parte_1_decodificador_1_p8, in_31, parte_1_decodificador_1_p10, in_32, parte_1_decodificador_1_p12, in_33, parte_1_decodificador_1_p14, in_34, parte_1_decodificador_1_p16
endmodule
