// Logisim project PARA TESTAR SE O DESLOCADOR DE 32 BITS COM SRE1 & SLL8 FUNCIONAM.circ as structural Verilog: 1 circuit, main circuit main
module main (
  input  in_1,
  input  in_2,
  input  in_3,
  input  in_4,
  input  in_5,
  input  in_6,
  input  in_7,
  input  in_8,
  input  in_9,
  input  in_10,
  input  in_11,
  input  in_12,
  input  in_13,
  input  in_14,
  input  in_15,
  input  in_16,
  input  in_17,
  input  in_18,
  input  in_19,
  input  in_20,
  input  in_21,
  input  in_22,
  input  in_23,
  input  in_24,
  input  in_25,
  input  in_26,
  input  in_27,
  input  in_28,
  input  in_29,
  input  in_30,
  input  in_31,
  input  in_32,
  input  SRA1,
  input  SLL8,
  output out_35,
  output out_36,
  output out_37,
  output out_38,
  output out_39,
  output out_40,
  output out_41,
  output out_42,
  output out_43,
  output out_44,
  output out_45,
  output out_46,
  output out_47,
  output out_48,
  output out_49,
  output out_50,
  output out_51,
  output out_52,
  output out_53,
  output out_54,
  output out_55,
  output out_56,
  output out_57,
  output out_58,
  output out_59,
  output out_60,
  output out_61,
  output out_62,
  output out_63,
  output out_64,
  output out_65,
  output out_66
);

  DESLOCADOR_COM_MUX_COMPLETO_DE_32_BITS_main main_1 (
    .SRA1(SRA1), .SLL8(SLL8), .in_3(in_1), .in_4(in_2), .in_5(in_3), .in_6(in_4), .in_7(in_5), .in_8(in_6),
    .in_9(in_7), .in_10(in_8), .in_11(in_9), .in_12(in_10), .in_13(in_11), .in_14(in_12), .in_15(in_13),
    .in_16(in_14), .in_17(in_15), .in_18(in_16), .in_19(in_17), .in_20(in_18), .in_21(in_19), .in_22(in_20),
    .in_23(in_21), .in_24(in_22), .in_25(in_23), .in_26(in_24), .in_27(in_25), .in_28(in_26), .in_29(in_27),
    .in_30(in_28), .in_31(in_29), .in_32(in_30), .in_33(in_31), .in_34(in_32), .out_35(out_35),
    .out_51(out_51), .out_36(out_36), .out_52(out_52), .out_37(out_37), .out_53(out_53), .out_38(out_38),
    .out_54(out_54), .out_39(out_39), .out_55(out_55), .out_40(out_40), .out_56(out_56), .out_41(out_41),
    .out_57(out_57), .out_42(out_42), .out_58(out_58), .out_43(out_43), .out_59(out_59), .out_44(out_44),
    .out_60(out_60), .out_45(out_45), .out_61(out_61), .out_46(out_46), .out_62(out_62), .out_47(out_47),
    .out_63(out_63), .out_48(out_48), .out_64(out_64), .out_49(out_49), .out_65(out_65), .out_50(out_50),
    .out_66(out_66));
endmodule
