// Logisim project chaves seletoras do decodificador.circ as structural Verilog: 1 circuit, main circuit parte_1_Decodificador
module parte_1_Decodificador (
  input  CONTROLL,
  input  A,
  input  B,
  input  C,
  input  D,
  input  E,
  input  F,
  input  G,
  input  H,
  input  I,
  input  J,
  input  K,
  input  L,
  input  M,
  input  N,
  input  O,
  input  P,
  input  Q,
  input  R,
  input  S,
  input  T,
  input  U,
  input  V,
  input  X,
  input  W,
  input  Y,
  input  Z,
  input  _1,
  input  _2,
  input  _3,
  input  _4,
  input  _5,
  input  _6,
  output out_34,
  output out_35,
  output out_36,
  output out_37,
  output out_38,
  output out_39,
  output out_40,
  output out_41,
  output out_42,
  output out_43,
  output out_44,
  output out_45,
  output out_46,
  output out_47,
  output out_48,
  output out_49,
  output out_50,
  output out_51,
  output out_52,
  output out_53,
  output out_54,
  output out_55,
  output out_56,
  output out_57,
  output out_58,
  output out_59,
  output out_60,
  output out_61,
  output out_62,
  output out_63,
  output out_64,
  output out_65
);

  wire main_1_c_2, main_1_enviando, main_2_c_2, main_2_env_1, main_2_env_2, main_2_env_3, main_2_env_4,
       main_2_env_5, main_2_env_6, main_2_env_7, main_2_env_8, main_2_enviando, main_3_c_2, main_3_env_1,
       main_3_env_2, main_3_env_3, main_3_env_4, main_3_env_5, main_3_env_6, main_3_env_7, main_3_env_8,
       main_3_enviando, main_4_env_1, main_4_env_2, main_4_env_3, main_4_env_4, main_4_env_5, main_4_env_6,
       main_4_env_7, main_4_env_8;

  parte1_main main_1 (
    .C(CONTROLL), .C_2(main_1_c_2), .ENVIANDO(main_1_enviando), .Receptor_1(main_2_env_1),
    .receptor_2(main_2_env_2), .receptor_3(main_2_env_3), .receptor_4(main_2_env_4),
    .receptor_5(main_2_env_5), .receptor_6(main_2_env_6), .receptor_7(main_2_env_7),
    .receptor_8(main_2_env_8), .in_1(A), .in_2(B), .in_3(C), .in_4(D), .in_5(E), .in_6(F), .in_7(G),
    .in_8(H), .out_20(out_34), .out_21(out_35), .out_22(out_36), .out_23(out_37), .out_24(out_38),
    .out_25(out_39), .out_26(out_40), .out_27(out_41));
  parte2_main main_2 (
    .C(main_1_c_2), .RCEBENDO(main_1_enviando), .env_1(main_2_env_1), .env_2(main_2_env_2),
    .env_3(main_2_env_3), .env_4(main_2_env_4), .env_5(main_2_env_5), .env_6(main_2_env_6),
    .env_7(main_2_env_7), .env_8(main_2_env_8), .C_2(main_2_c_2), .ENVIANDO(main_2_enviando),
    .receptor_1(main_3_env_1), .receptor_2(main_3_env_2), .receptor_3(main_3_env_3),
    .receptor_4(main_3_env_4), .receptor_5(main_3_env_5), .receptor_6(main_3_env_6),
    .receptor_7(main_3_env_7), .receptor_8(main_3_env_8), .in_1(I), .in_2(J), .in_3(K), .in_4(L), .in_5(M),
    .in_6(N), .in_7(O), .in_8(P), .out_24(out_42), .out_25(out_43), .out_26(out_44), .out_27(out_45),
    .out_28(out_46), .out_29(out_47), .out_30(out_48), .out_31(out_49));
  parte2_main main_3 (
    .C(main_2_c_2), .RCEBENDO(main_2_enviando), .env_1(main_3_env_1), .env_2(main_3_env_2),
    .env_3(main_3_env_3), .env_4(main_3_env_4), .env_5(main_3_env_5), .env_6(main_3_env_6),
    .env_7(main_3_env_7), .env_8(main_3_env_8), .C_2(main_3_c_2), .ENVIANDO(main_3_enviando),
    .receptor_1(main_4_env_1), .receptor_2(main_4_env_2), .receptor_3(main_4_env_3),
    .receptor_4(main_4_env_4), .receptor_5(main_4_env_5), .receptor_6(main_4_env_6),
    .receptor_7(main_4_env_7), .receptor_8(main_4_env_8), .in_1(Q), .in_2(R), .in_3(S), .in_4(T), .in_5(U),
    .in_6(V), .in_7(X), .in_8(W), .out_24(out_50), .out_25(out_51), .out_26(out_52), .out_27(out_53),
    .out_28(out_54), .out_29(out_55), .out_30(out_56), .out_31(out_57));
  parte4_main main_4 (
    .C(main_3_c_2), .RCEBENDO(main_3_enviando), .env_1(main_4_env_1), .env_2(main_4_env_2),
    .env_3(main_4_env_3), .env_4(main_4_env_4), .env_5(main_4_env_5), .env_6(main_4_env_6),
    .env_7(main_4_env_7), .env_8(main_4_env_8), .in_1(Y), .in_2(Z), .in_3(_1), .in_4(_2), .in_5(_3),
    .in_6(_4), .in_7(_5), .in_8(_6), .out_14(out_58), .out_15(out_59), .out_16(out_60), .out_17(out_61),
    .out_18(out_62), .out_19(out_63), .out_20(out_64), .out_21(out_65));
endmodule
