// Logisim project decodificador.circ as structural Verilog
module chaves_seletoras (
  input  IN,
  input  OUT,
  input  SRA1,
  input  SLL8,
  output C,
  output OUT_2
);

  wire xor_1_out;

  Multiplexer multiplexer_1 (.in0(IN), .in1(OUT), .out(OUT_2), .sel(xor_1_out));  // open: en
  xor xor_1 (xor_1_out, SRA1, SLL8);

  assign C = SRA1;
endmodule
