// Logisim project filtro das chaves seletoras_with_head.circ as structural Verilog: 1 circuit, main circuit main
module main (
  input  IN,
  input  IN_2,
  input  IN_3,
  input  IN_4,
  input  OUT,
  input  OUT_2,
  input  OUT_3,
  input  OUT_4,
  input  SRA1,
  input  SLL8,
  input  IN_5,
  input  IN_6,
  input  IN_7,
  input  IN_8,
  input  OUT_5,
  input  OUT_6,
  input  OUT_7,
  input  OUT_8,
  input  IN_9,
  input  IN_10,
  input  IN_11,
  input  IN_12,
  input  OUT_9,
  input  OUT_10,
  input  OUT_11,
  input  OUT_12,
  input  IN_13,
  input  IN_14,
  input  IN_15,
  input  IN_16,
  input  OUT_13,
  input  OUT_14,
  input  OUT_15,
  input  OUT_16,
  output C,
  output OUTPUT,
  output OUTPUT_2,
  output OUTPUT_3,
  output OUTPUT_4,
  output OUTPUT_5,
  output OUTPUT_6,
  output OUTPUT_7,
  output OUTPUT_8,
  output OUTPUT_9,
  output OUTPUT_10,
  output OUTPUT_11,
  output OUTPUT_12,
  output OUTPUT_13,
  output OUTPUT_14,
  output OUTPUT_15,
  output OUTPUT_16
);

  wire xor_1_out;

  xor xor_1 (xor_1_out, SRA1, SLL8);
  Multiplexer multiplexer_1 (.in0(IN), .in1(OUT), .out(OUTPUT), .sel(xor_1_out));  // open: en
  Multiplexer multiplexer_2 (.in0(IN_5), .in1(OUT_5), .out(OUTPUT_5), .sel(xor_1_out));  // open: en
  Multiplexer multiplexer_3 (.in0(IN_9), .in1(OUT_9), .out(OUTPUT_9), .sel(xor_1_out));  // open: en
  Multiplexer multiplexer_4 (.in0(IN_13), .in1(OUT_13), .out(OUTPUT_13), .sel(xor_1_out));  // open: en
  Multiplexer multiplexer_5 (.in0(IN_2), .in1(OUT_2), .out(OUTPUT_2), .sel(xor_1_out));  // open: en
  Multiplexer multiplexer_6 (.in0(IN_6), .in1(OUT_6), .out(OUTPUT_6), .sel(xor_1_out));  // open: en
  Multiplexer multiplexer_7 (.in0(IN_10), .in1(OUT_10), .out(OUTPUT_10), .sel(xor_1_out));  // open: en
  Multiplexer multiplexer_8 (.in0(IN_14), .in1(OUT_14), .out(OUTPUT_14), .sel(xor_1_out));  // open: en
  Multiplexer multiplexer_9 (.in0(IN_3), .in1(OUT_3), .out(OUTPUT_3), .sel(xor_1_out));  // open: en
  Multiplexer multiplexer_10 (.in0(IN_7), .in1(OUT_7), .out(OUTPUT_7), .sel(xor_1_out));  // open: en
  Multiplexer multiplexer_11 (.in0(IN_11), .in1(OUT_11), .out(OUTPUT_11), .sel(xor_1_out));  // open: en
  Multiplexer multiplexer_12 (.in0(IN_15), .in1(OUT_15), .out(OUTPUT_15), .sel(xor_1_out));  // open: en
  Multiplexer multiplexer_13 (.in0(IN_4), .in1(OUT_4), .out(OUTPUT_4), .sel(xor_1_out));  // open: en
  Multiplexer multiplexer_14 (.in0(IN_8), .in1(OUT_8), .out(OUTPUT_8), .sel(xor_1_out));  // open: en
  Multiplexer multiplexer_15 (.in0(IN_12), .in1(OUT_12), .out(OUTPUT_12), .sel(xor_1_out));  // open: en
  Multiplexer multiplexer_16 (.in0(IN_16), .in1(OUT_16), .out(OUTPUT_16), .sel(xor_1_out));  // open: en

  assign C = SRA1;
endmodule
