// Logisim project parte1.circ as structural Verilog: 1 circuit, main circuit main
module main (
  input  in_1,
  input  in_2,
  input  in_3,
  input  in_4,
  input  in_5,
  input  in_6,
  input  in_7,
  input  in_8,
  input  C,
  input  Receptor_1,
  input  receptor_2,
  input  receptor_3,
  input  receptor_4,
  input  receptor_5,
  input  receptor_6,
  input  receptor_7,
  input  receptor_8,
  output C_2,
  output ENVIANDO,
  output out_20,
  output out_21,
  output out_22,
  output out_23,
  output out_24,
  output out_25,
  output out_26,
  output out_27
);

  wire and_1_out, and_3_out, and_5_out, and_7_out, and_9_out, and_11_out, and_14_out, not_1_out;

  not not_1 (not_1_out, C);
  and and_1 (and_1_out, in_1, C);
  // AND_Gate and_2 has open pins: in0=not_1_out, in1=in_2, out=open
  and and_3 (and_3_out, in_2, C);
  or or_1 (out_21, and_1_out, receptor_2);
  // AND_Gate and_4 has open pins: in0=not_1_out, in1=in_3, out=open
  or or_2 (out_22, and_3_out, receptor_3);
  and and_5 (and_5_out, in_3, C);
  // AND_Gate and_6 has open pins: in0=not_1_out, in1=in_4, out=open
  and and_7 (and_7_out, in_4, C);
  or or_3 (out_23, and_5_out, receptor_4);
  // AND_Gate and_8 has open pins: in0=not_1_out, in1=in_5, out=open
  or or_4 (out_24, and_7_out, receptor_5);
  and and_9 (and_9_out, in_5, C);
  // AND_Gate and_10 has open pins: in0=not_1_out, in1=in_6, out=open
  and and_11 (and_11_out, in_6, C);
  or or_5 (out_25, and_9_out, receptor_6);
  // AND_Gate and_12 has open pins: in0=not_1_out, in1=in_7, out=open
  or or_6 (out_26, and_11_out, receptor_7);
  // AND_Gate and_13 has open pins: in0=not_1_out, in1=in_8, out=open
  and and_14 (and_14_out, in_7, C);
  and and_15 (ENVIANDO, in_8, C);
  or or_7 (out_27, and_14_out, receptor_8);

  assign C_2 = C;
  assign out_20 = Receptor_1;
endmodule
