// Logisim project parte2.circ as structural Verilog: 1 circuit, main circuit main
module main (
  input  in_1,
  input  in_2,
  input  in_3,
  input  in_4,
  input  in_5,
  input  in_6,
  input  in_7,
  input  in_8,
  input  C,
  input  receptor_1,
  input  RCEBENDO,
  input  receptor_2,
  input  receptor_3,
  input  receptor_4,
  input  receptor_5,
  input  receptor_6,
  input  receptor_7,
  input  receptor_8,
  output C_2,
  output ENVIANDO,
  output env_1,
  output env_2,
  output env_3,
  output out_24,
  output out_25,
  output out_26,
  output out_27,
  output out_28,
  output out_29,
  output out_30,
  output out_31,
  output env_4,
  output env_5,
  output env_6,
  output env_7,
  output env_8
);

  wire and_1_out, and_4_out, and_6_out, and_8_out, and_9_out, and_12_out, and_14_out, not_1_out;

  not not_1 (not_1_out, C);
  and and_1 (and_1_out, in_1, C);
  and and_2 (env_1, not_1_out, in_1);
  or or_1 (out_24, RCEBENDO, receptor_1);
  and and_3 (env_2, not_1_out, in_2);
  and and_4 (and_4_out, in_2, C);
  or or_2 (out_25, and_1_out, receptor_2);
  and and_5 (env_3, not_1_out, in_3);
  and and_6 (and_6_out, in_3, C);
  or or_3 (out_26, and_4_out, receptor_3);
  and and_7 (env_4, not_1_out, in_4);
  and and_8 (and_8_out, in_4, C);
  or or_4 (out_27, and_6_out, receptor_4);
  and and_9 (and_9_out, in_5, C);
  and and_10 (env_5, not_1_out, in_5);
  or or_5 (out_28, and_8_out, receptor_5);
  and and_11 (env_6, not_1_out, in_6);
  and and_12 (and_12_out, in_6, C);
  or or_6 (out_29, and_9_out, receptor_6);
  and and_13 (env_7, not_1_out, in_7);
  and and_14 (and_14_out, in_7, C);
  or or_7 (out_30, and_12_out, receptor_7);
  and and_15 (env_8, not_1_out, in_8);
  or or_8 (out_31, and_14_out, receptor_8);
  and and_16 (ENVIANDO, in_8, C);

  assign C_2 = C;
endmodule
